// Logisim project ActualCPU.circ as structural Verilog: 1 circuit, main circuit main
module main (
);

  wire and_1_out, not_1_out;
  wire [7:0] Address_Counter_q, MAIN_data, MicroCode_data, pull_resistor_1_node;

  Counter Address_Counter (.Q(Address_Counter_q));  // open: clr, load, up, count, clk, D, carry
  ROM MAIN (.addr(Address_Counter_q), .data(MAIN_data));
  not not_1 (not_1_out, Address_Counter_q[6]);
  and and_1 (and_1_out, Address_Counter_q[7], not_1_out);
  Pull_Resistor pull_resistor_1 (.node(pull_resistor_1_node[0]));
  Transistor transistor_1 (.in(MAIN_data[0]), .out(pull_resistor_1_node[0]), .gate(Address_Counter_q[7]));
  Pull_Resistor pull_resistor_2 (.node(pull_resistor_1_node[1]));
  Transistor transistor_2 (.in(MAIN_data[1]), .out(pull_resistor_1_node[1]), .gate(Address_Counter_q[7]));
  Pull_Resistor pull_resistor_3 (.node(pull_resistor_1_node[2]));
  Transistor transistor_3 (.in(MAIN_data[2]), .out(pull_resistor_1_node[2]), .gate(Address_Counter_q[7]));
  RAM ram_1 (.addr(Address_Counter_q), .oe(and_1_out), .dout(pull_resistor_1_node));  // open: we, clk, din
  Pull_Resistor pull_resistor_4 (.node(pull_resistor_1_node[3]));
  Transistor transistor_4 (.in(MAIN_data[3]), .out(pull_resistor_1_node[3]), .gate(Address_Counter_q[7]));
  Pull_Resistor pull_resistor_5 (.node(pull_resistor_1_node[4]));
  Transistor transistor_5 (.in(MAIN_data[4]), .out(pull_resistor_1_node[4]), .gate(Address_Counter_q[7]));
  Pull_Resistor pull_resistor_6 (.node(pull_resistor_1_node[5]));
  Transistor transistor_6 (.in(MAIN_data[5]), .out(pull_resistor_1_node[5]), .gate(Address_Counter_q[7]));
  Pull_Resistor pull_resistor_7 (.node(pull_resistor_1_node[6]));
  Transistor transistor_7 (.in(MAIN_data[6]), .out(pull_resistor_1_node[6]), .gate(Address_Counter_q[7]));
  Pull_Resistor pull_resistor_8 (.node(pull_resistor_1_node[7]));
  Transistor transistor_8 (.in(MAIN_data[7]), .out(pull_resistor_1_node[7]), .gate(Address_Counter_q[7]));
  Register A ();  // open: D, en, clk, Q, clr
  Register B ();  // open: D, en, clk, Q, clr
  ROM MicroCode (.data(MicroCode_data));  // open: addr
  Counter Program_Counter ();  // open: clr, load, up, count, clk, D, carry, Q

  // Notes on the sheet:
  //   contents of MAIN (hex, n*v repeats v):
  //   fa
  //   ROM OUTPUT ENABLE
  //   ROM OUT
  //   RAM OUT
  //   Microcode
endmodule
